// Logisim project B C + A B.circ as structural Verilog: 1 circuit, main circuit main
module main (
  input  A,
  input  B,
  input  C,
  output Q
);

  wire and_1_out, and_2_out, and_3_out, or_1_out;

  and and_1 (and_1_out, A, B);
  and and_2 (and_2_out, C, B);
  or or_1 (or_1_out, B, C);
  and and_3 (and_3_out, or_1_out, and_2_out);
  or or_2 (Q, and_1_out, and_3_out);

  // Notes on the sheet:
  //   AB
  //   BC
  //   B+C
endmodule
