// Logisim project Comparator.circ as structural Verilog: 1 circuit, main circuit main
module main (
  input  [7:0] in_1,
  input  [7:0] in_2,
  input  in_3,
  input  A0,
  input  B0,
  input  A1,
  input  B1,
  input  A2,
  input  B2,
  input  A3,
  input  B3,
  output out_12
);

  wire adder_1_cout, adder_1_out, adder_2_cout, adder_2_out, adder_3_cout, adder_3_out, adder_4_out,
       comparator_1_eq, comparator_1_gt, comparator_1_lt;

  Comparator comparator_1 (.a(in_1), .b(in_2), .gt(comparator_1_gt), .eq(comparator_1_eq), .lt(comparator_1_lt));
  Adder #(.width(1)) adder_1 (.a(A0), .b(B0), .out(adder_1_out), .cin(in_3), .cout(adder_1_cout));
  Adder #(.width(1)) adder_2 (.a(A1), .b(B1), .out(adder_2_out), .cin(adder_1_cout), .cout(adder_2_cout));
  Adder #(.width(1)) adder_3 (.a(A2), .b(B2), .out(adder_3_out), .cin(adder_2_cout), .cout(adder_3_cout));
  Adder #(.width(1)) adder_4 (.a(A3), .b(B3), .out(adder_4_out), .cin(adder_3_cout), .cout(out_12));
  LED led_1 (.in(comparator_1_gt));
  LED led_2 (.in(comparator_1_eq));
  LED led_3 (.in(comparator_1_lt));
endmodule
