// Logisim project Encoder and Decoder.circ as structural Verilog: 1 circuit, main circuit main
module main (
  input  _0,
  input  _1,
  input  _2,
  input  in_4,
  input  _3,
  input  _0_2,
  input  _1_2,
  input  _2_2,
  input  _3_2,
  input  _4,
  input  _5,
  input  _6,
  input  in_13,
  input  _7,
  input  [1:0] in_15,
  input  [2:0] in_16,
  output [1:0] out_17,
  output [2:0] out_18
);

  wire decoder_1_out0, decoder_1_out1, decoder_1_out2, decoder_1_out3, decoder_2_out0, decoder_2_out1,
       decoder_2_out2, decoder_2_out3, decoder_2_out4, decoder_2_out5, decoder_2_out6, decoder_2_out7;

  Priority_Encoder #(.select(2)) priority_encoder_1 (
    .in0(_0), .in1(_1), .in2(_2), .in3(_3), .out(out_17), .en_in(in_4));  // open: gs, en_out
  Priority_Encoder priority_encoder_2 (
    .in0(_0_2), .in1(_1_2), .in2(_2_2), .in3(_3_2), .in4(_4), .in5(_5), .in6(_6), .in7(_7), .out(out_18),
    .en_in(in_13));  // open: gs, en_out
  Decoder #(.select(2)) decoder_1 (
    .out0(decoder_1_out0), .out1(decoder_1_out1), .out2(decoder_1_out2), .out3(decoder_1_out3), .sel(in_15));  // open: en
  Decoder #(.select(3)) decoder_2 (
    .out0(decoder_2_out0), .out1(decoder_2_out1), .out2(decoder_2_out2), .out3(decoder_2_out3),
    .out4(decoder_2_out4), .out5(decoder_2_out5), .out6(decoder_2_out6), .out7(decoder_2_out7), .sel(in_16));  // open: en
  LED u__0 (.in(decoder_1_out0));
  LED u__1 (.in(decoder_1_out1));
  LED u__2 (.in(decoder_1_out2));
  LED u__3 (.in(decoder_1_out3));
  LED led_1 (.in(decoder_2_out0));
  LED led_2 (.in(decoder_2_out1));
  LED led_3 (.in(decoder_2_out2));
  LED led_4 (.in(decoder_2_out3));
  LED led_5 (.in(decoder_2_out4));
  LED led_6 (.in(decoder_2_out5));
  LED led_7 (.in(decoder_2_out6));
  LED led_8 (.in(decoder_2_out7));
endmodule
