// Logisim project Exp 1 All Gates.circ as structural Verilog: 1 circuit, main circuit main
module main (
  input  A,
  input  A_2,
  input  B,
  input  A_3,
  input  B_2,
  input  A_4,
  input  B_3,
  input  A_5,
  input  B_4,
  input  A_6,
  input  B_5,
  input  A_7,
  input  B_6,
  output Y,
  output Y_2,
  output Y_3,
  output Y_4,
  output Y_5,
  output Y_6,
  output Y_7
);

  not not_1 (Y, A);
  and and_1 (Y_2, A_2, B);
  nand nand_1 (Y_3, A_3, B_2);
  or or_1 (Y_4, A_4, B_3);
  nor nor_1 (Y_5, A_5, B_4);
  xor xor_1 (Y_6, A_6, B_5);
  xnor xnor_1 (Y_7, A_7, B_6);

  // Notes on the sheet:
  //   NOT
  //   AND
  //   NAND
  //   OR
  //   NOR
  //   XOR
  //   XNOR
endmodule
