// Logisim project Exp 3 Half Adder.circ as structural Verilog: 1 circuit, main circuit main
module main (
  input  in_1,
  input  in_2,
  output Sum,
  output C_Out
);

  and and_1 (C_Out, in_1, in_2);
  xor xor_1 (Sum, in_1, in_2);

  // Notes on the sheet:
  //   XOR1
  //   AND1
endmodule
