// Logisim project Exp 5 D flip flop.circ as structural Verilog: 1 circuit, main circuit main
module main (
  input  D,
  output Q,
  output Q_bar
);

  wire Clock_out;

  Clock Clock (.out(Clock_out));
  D_Flip_Flop d_ff_1 (.clk(Clock_out), .D(D), .Q(Q), .Qn(Q_bar));  // open: preset, en, reset
endmodule
