// Logisim project Exp 5 JK flip flop.circ as structural Verilog: 1 circuit, main circuit main
module main (
  input  J,
  input  K,
  output Q,
  output nQ
);

  wire Clock_out, nand_1_out, nand_2_out;

  Clock Clock (.out(Clock_out));
  nand nand_1 (nand_1_out, nQ, J, Clock_out);
  nand nand_2 (nand_2_out, Clock_out, K, Q);
  nand nand_3 (Q, nand_1_out, nQ);
  nand nand_4 (nQ, Q, nand_2_out);
endmodule
