// Logisim project Exp 5 SR flip flop.circ as structural Verilog: 1 circuit, main circuit main
module main (
  input  S,
  input  R,
  output Q,
  output Q_bar
);

  wire Clock_out, nand_1_out, nand_2_out;

  Clock Clock (.out(Clock_out));
  nand nand_1 (nand_1_out, S, Clock_out);
  nand nand_2 (nand_2_out, Clock_out, R);
  nand nand_3 (Q, nand_1_out, Q_bar);
  nand nand_4 (Q_bar, Q, nand_2_out);
endmodule
