// Logisim project Exp 5 T flip flop.circ as structural Verilog: 1 circuit, main circuit main
module main (
  input  T,
  output PRESET,
  output out_3,
  output out_4,
  output CLEAR
);

  wire CLK_out;

  Clock CLK (.out(CLK_out));
  J_K_Flip_Flop j_k_ff_1 (.J(T), .clk(CLK_out), .K(T), .Q(out_3), .Qn(out_4), .en(CLEAR));  // open: preset, reset
endmodule
