// Logisim project Exp 6 PISO Shift.circ as structural Verilog: 1 circuit, main circuit main
module main (
  input  D3,
  input  D2,
  input  D1,
  input  D0,
  input  Shift_Load,
  input  CLR,
  output Q0
);

  wire and_1_out, and_2_out, and_3_out, and_4_out, and_5_out, and_6_out, CLK_out, d_ff_1_q, d_ff_2_q,
       d_ff_3_q, not_1_out, or_1_out, or_2_out, or_3_out;

  Clock CLK (.out(CLK_out));
  not not_1 (not_1_out, Shift_Load);
  and and_1 (and_1_out, d_ff_1_q, Shift_Load);
  D_Flip_Flop d_ff_1 (.clk(CLK_out), .D(D3), .Q(d_ff_1_q), .reset(CLR));  // open: Qn, preset, en
  and and_2 (and_2_out, not_1_out, D2);
  or or_1 (or_1_out, and_1_out, and_2_out);
  and and_3 (and_3_out, d_ff_2_q, Shift_Load);
  D_Flip_Flop d_ff_2 (.clk(CLK_out), .D(or_1_out), .Q(d_ff_2_q), .reset(CLR));  // open: Qn, preset, en
  and and_4 (and_4_out, not_1_out, D1);
  or or_2 (or_2_out, and_3_out, and_4_out);
  D_Flip_Flop d_ff_3 (.clk(CLK_out), .D(or_2_out), .Q(d_ff_3_q), .reset(CLR));  // open: Qn, preset, en
  and and_5 (and_5_out, d_ff_3_q, Shift_Load);
  or or_3 (or_3_out, and_5_out, and_6_out);
  and and_6 (and_6_out, not_1_out, D0);
  D_Flip_Flop d_ff_4 (.clk(CLK_out), .D(or_3_out), .Q(Q0), .reset(CLR));  // open: Qn, preset, en

  // Notes on the sheet:
  //   PISO Shift
  //   Register
endmodule
