// Logisim project Exp 6 SIPO Shift.circ as structural Verilog: 1 circuit, main circuit main
module main (
  input  D3,
  input  PR,
  input  CLR,
  output Q3,
  output Q2,
  output Q1,
  output Q0
);

  wire CLK_out;

  Clock CLK (.out(CLK_out));
  D_Flip_Flop d_ff_1 (.clk(CLK_out), .D(D3), .Q(Q3), .preset(PR), .reset(CLR));  // open: Qn, en
  D_Flip_Flop d_ff_2 (.clk(CLK_out), .D(Q3), .Q(Q2), .preset(PR), .reset(CLR));  // open: Qn, en
  D_Flip_Flop d_ff_3 (.clk(CLK_out), .D(Q2), .Q(Q1), .preset(PR), .reset(CLR));  // open: Qn, en
  D_Flip_Flop d_ff_4 (.clk(CLK_out), .D(Q1), .Q(Q0), .preset(PR), .reset(CLR));  // open: Qn, en

  // Notes on the sheet:
  //   SIPO Shift
  //   Register
endmodule
