// Logisim project Exp 7 Asynchronous Up Counter.circ as structural Verilog: 1 circuit, main circuit main
module main (
  input  in_1,
  output Q3,
  output Q2,
  output Q1,
  output Q0
);

  wire CLK_out;

  Clock CLK (.out(CLK_out));
  J_K_Flip_Flop #(.trigger("falling")) FF0 (.J(in_1), .clk(CLK_out), .K(in_1), .Q(Q3));  // open: Qn, preset, en, reset
  J_K_Flip_Flop #(.trigger("falling")) FF1 (.J(in_1), .clk(Q3), .K(in_1), .Q(Q2));  // open: Qn, preset, en, reset
  J_K_Flip_Flop #(.trigger("falling")) FF2 (.J(in_1), .clk(Q2), .K(in_1), .Q(Q1));  // open: Qn, preset, en, reset
  J_K_Flip_Flop #(.trigger("falling")) FF3 (.J(in_1), .clk(Q1), .K(in_1), .Q(Q0));  // open: Qn, preset, en, reset
endmodule
