// Logisim project Extra.circ as structural Verilog: 1 circuit, main circuit main
module main (
  input  A,
  input  A_2,
  input  A_3,
  input  A_4,
  input  B,
  input  B_2,
  input  A_5,
  input  A_6,
  input  B_3,
  input  B_4,
  output Y,
  output Y_2,
  output Y_3,
  output Y_4,
  output Y_5,
  output Y_6
);

  wire nand_1_out, nand_3_out, nand_4_out, nor_1_out, nor_3_out, nor_4_out;

  nand nand_1 (nand_1_out, A_4, B);
  nand nand_2 (Y_2, A_2, A_2);
  nand nand_3 (nand_3_out, A_5, A_5);
  nand nand_4 (nand_4_out, B_4, B_4);
  nand nand_5 (Y_4, nand_1_out, nand_1_out);
  nand nand_6 (Y_6, nand_3_out, nand_4_out);
  nor nor_1 (nor_1_out, A_6, B_3);
  nor nor_2 (Y, A, A);
  nor nor_3 (nor_3_out, A_3, A_3);
  nor nor_4 (nor_4_out, B_2, B_2);
  nor nor_5 (Y_5, nor_1_out, nor_1_out);
  nor nor_6 (Y_3, nor_3_out, nor_4_out);
endmodule
