// Logisim project JK flip flop Memory.circ as structural Verilog: 1 circuit, main circuit main
module main (
  input  J,
  input  K,
  input  PRE,
  input  EN,
  input  CLR,
  output Q,
  output Q_bar
);

  wire Clock_out;

  Clock Clock (.out(Clock_out));
  J_K_Flip_Flop j_k_ff_1 (.J(J), .clk(Clock_out), .K(K), .Q(Q), .Qn(Q_bar), .preset(PRE), .en(EN), .reset(CLR));
endmodule
