// Logisim project MUX and DMX.circ as structural Verilog: 1 circuit, main circuit main
module main (
  input  I0,
  input  I1,
  input  I2,
  input  I3,
  input  I0_2,
  input  I4,
  input  I5,
  input  I1_2,
  input  I6,
  input  I7,
  input  S,
  input  in_12,
  input  in_13,
  input  [2:0] in_14,
  input  I0_3,
  input  I1_3,
  input  in_17,
  input  I2_2,
  input  in_19,
  input  I3_2,
  input  in_21,
  input  in_22,
  input  [1:0] SOS1,
  input  in_24,
  input  in_25,
  input  in_26,
  input  in_27,
  input  in_28,
  input  [3:0] in_29,
  input  in_30,
  input  in_31,
  input  in_32,
  input  in_33,
  input  S_2,
  input  in_35,
  input  in_36,
  input  in_37,
  input  [1:0] in_38
);

  wire demultiplexer_1_out0, demultiplexer_1_out1, demultiplexer_2_out0, demultiplexer_2_out1,
       demultiplexer_2_out2, demultiplexer_2_out3, multiplexer_1_out, multiplexer_2_out, multiplexer_3_out,
       multiplexer_4_out;

  Demultiplexer demultiplexer_1 (
    .out0(demultiplexer_1_out0), .out1(demultiplexer_1_out1), .in(in_30), .sel(S_2));  // open: en
  Demultiplexer #(.select(2)) demultiplexer_2 (
    .out0(demultiplexer_2_out0), .out1(demultiplexer_2_out1), .out2(demultiplexer_2_out2),
    .out3(demultiplexer_2_out3), .in(in_37), .sel(in_38));  // open: en
  LED led_1 (.in(demultiplexer_1_out0));
  LED led_2 (.in(demultiplexer_1_out1));
  Multiplexer multiplexer_1 (.in0(I0_2), .in1(I1_2), .out(multiplexer_1_out), .sel(S));  // open: en
  LED led_3 (.in(multiplexer_1_out));
  Multiplexer #(.select(2)) multiplexer_2 (
    .in0(I0_3), .in1(I1_3), .in2(I2_2), .in3(I3_2), .out(multiplexer_2_out), .sel(SOS1));  // open: en
  LED led_4 (.in(multiplexer_2_out));
  LED led_5 (.in(demultiplexer_2_out0));
  LED led_6 (.in(demultiplexer_2_out1));
  LED led_7 (.in(demultiplexer_2_out2));
  LED led_8 (.in(demultiplexer_2_out3));
  Multiplexer #(.select(3)) multiplexer_3 (
    .in0(I0), .in1(I1), .in2(I2), .in3(I3), .in4(I4), .in5(I5), .in6(I6), .in7(I7), .out(multiplexer_3_out),
    .sel(in_14));  // open: en
  Multiplexer #(.select(4)) multiplexer_4 (
    .in0(in_12), .in1(in_13), .in2(in_17), .in3(in_19), .in4(in_21), .in5(in_22), .in6(in_24), .in7(in_25),
    .in8(in_26), .in9(in_27), .in10(in_28), .in11(in_31), .in12(in_32), .in13(in_33), .in14(in_35),
    .in15(in_36), .out(multiplexer_4_out), .sel(in_29));  // open: en
  LED led_9 (.in(multiplexer_3_out));
  LED led_10 (.in(multiplexer_4_out));

  // Notes on the sheet:
  //   Y0
  //   Y1
  //   Y0
  //   Y1
  //   Y2
  //   Y3
endmodule
