// Logisim project Problem 1.circ as structural Verilog: 1 circuit, main circuit main
module main (
  input  A,
  input  B,
  output Z
);

  wire and_1_out, not_1_out, or_1_out;

  not not_1 (not_1_out, A);
  or or_1 (or_1_out, A, B);
  and and_1 (and_1_out, not_1_out, or_1_out);
  or or_2 (Z, and_1_out, or_1_out);
endmodule
