// Logisim project Problem 2.circ as structural Verilog: 1 circuit, main circuit main
module main (
  input  x,
  input  y,
  output O
);

  wire and_1_out, and_2_out, not_1_out, not_2_out;

  not not_1 (not_1_out, x);
  not not_2 (not_2_out, y);
  and and_1 (and_1_out, y, not_1_out);
  and and_2 (and_2_out, not_2_out, x);
  or or_1 (O, and_1_out, and_2_out);
endmodule
