// Logisim project Problem 6.circ as structural Verilog: 1 circuit, main circuit main
module main (
  input  A,
  input  B,
  input  C,
  output X
);

  wire and_1_out, and_2_out, and_3_out;

  and and_1 (and_1_out, A, B);
  and and_2 (and_2_out, A, B, C);
  and and_3 (and_3_out, A, B, C);
  or or_1 (X, and_1_out, and_2_out, and_3_out);

  // Notes on the sheet:
  //   D=A.B
  //   E=A.C
  //   F=A.B.C
endmodule
