// Logisim project ~(A B) B ~C.circ as structural Verilog: 1 circuit, main circuit main
module main (
  input  A,
  input  B,
  input  C,
  output Y
);

  wire nand_1_out, not_1_out;

  nand nand_1 (nand_1_out, A, B);
  not not_1 (not_1_out, C);
  and and_1 (Y, nand_1_out, B, not_1_out);
endmodule
