// Logisim project Exp 2 F1.circ as structural Verilog: 1 circuit, main circuit main
module main (
  input  A,
  input  B,
  output AB_AB
);

  wire and_1_out, and_2_out, not_1_out;

  not not_1 (not_1_out, A);
  and and_1 (and_1_out, not_1_out, B);
  and and_2 (and_2_out, B, A);
  or or_1 (AB_AB, and_1_out, and_2_out);

  // Notes on the sheet:
  //   _
  //   AB
  //   AB
  //   _
endmodule
