// Logisim project Problem 5.circ as structural Verilog: 1 circuit, main circuit main
module main (
  input  A,
  input  B,
  input  C,
  input  D,
  output Z
);

  wire and_1_out, not_1_out, not_2_out, or_1_out, xor_1_out, xor_2_out;

  not not_1 (not_1_out, D);
  xor xor_1 (xor_1_out, A, D);
  and and_1 (and_1_out, A, not_1_out);
  or or_1 (or_1_out, C, xor_1_out);
  xor xor_2 (xor_2_out, and_1_out, B);
  not not_2 (not_2_out, or_1_out);
  or or_2 (Z, xor_2_out, not_2_out);
endmodule
